# Fritzing sketch grblshield_bluepillv3_groundfill (saved by Fritzing 0.9.10b)
circuit board: 9.77301cm x 9.86238cm
breadboards: 1

parts:
  bluepill = STM32F103C8T6 blue mini board
  A11 = female pin header, 1 pin [form="♀ (female)"]
  A12 = female pin header, 1 pin [form="♀ (female)"]
  COOLANT = female pin header, 2 pins [form="♀ (female)"]
  GND = female pin header, 1 pin [form="♀ (female)"]
  5V = female pin header, 1 pin [form="♀ (female)"]
  - = female pin header, 1 pin [form="♀ (female)"]
  DOOR = female pin header, 1 pin [form="♀ (female)"]
  CYCLE_STRT = female pin header, 1 pin [form="♀ (female)"]
  FEED_HLD = female pin header, 1 pin [form="♀ (female)"]
  CTRL_RESET = female pin header, 1 pin [form="♀ (female)"]
  X = female pin header, 1 pin [form="♀ (female)"]
  Y-L = female pin header, 1 pin [form="♀ (female)"]
  Z = female pin header, 1 pin [form="♀ (female)"]
  Y-R = female pin header, 1 pin [form="♀ (female)"]
  74LS08_(AND) = IC, DIP package, 14 pins [chip_label=IC]
  74LS32_(OR) = IC, DIP package, 14 pins [chip_label=IC]
  74245 = IC, DIP package, 20 pins [chip_label=IC]
  RST = female pin header, 1 pin [form="♀ (female)"]
  B11 = female pin header, 1 pin [form="♀ (female)"]
  B10 = female pin header, 1 pin [form="♀ (female)"]
  VBAT = female pin header, 1 pin [form="♀ (female)"]
  C6 = Electrolytic Capacitor [capacitance=1µF voltage=35V package="100 mil [THT, electrolytic]"]
  GND_2 = female pin header, 1 pin [form="♀ (female)"]
  EN = female pin header, 1 pin [form="♀ (female)"]
  DIR = female pin header, 1 pin [form="♀ (female)"]
  STEP = female pin header, 1 pin [form="♀ (female)"]
  EN_2 = female pin header, 1 pin [form="♀ (female)"]
  DIR_2 = female pin header, 1 pin [form="♀ (female)"]
  GND_3 = female pin header, 1 pin [form="♀ (female)"]
  GND_4 = female pin header, 1 pin [form="♀ (female)"]
  EN_3 = female pin header, 1 pin [form="♀ (female)"]
  DIR_3 = female pin header, 1 pin [form="♀ (female)"]
  STEP_2 = female pin header, 1 pin [form="♀ (female)"]
  GND_5 = female pin header, 1 pin [form="♀ (female)"]
  EN_4 = female pin header, 1 pin [form="♀ (female)"]
  DIR_4 = female pin header, 1 pin [form="♀ (female)"]
  STEP_3 = female pin header, 1 pin [form="♀ (female)"]
  GND_6 = female pin header, 1 pin [form="♀ (female)"]
  EN_5 = female pin header, 1 pin [form="♀ (female)"]
  DIR_5 = female pin header, 1 pin [form="♀ (female)"]
  STEP_4 = female pin header, 1 pin [form="♀ (female)"]
  C7 = Electrolytic Capacitor [capacitance=1µF voltage=35V package="100 mil [THT, electrolytic]"]
  74245_2 = IC, DIP package, 20 pins [chip_label=IC]
  GND_7 = female pin header, 1 pin [form="♀ (female)"]
  VCC = female pin header, 1 pin [form="♀ (female)"]
  VCC_2 = female pin header, 1 pin [form="♀ (female)"]
  GND_8 = female pin header, 1 pin [form="♀ (female)"]
  VCC_3 = female pin header, 1 pin [form="♀ (female)"]
  GND_9 = female pin header, 1 pin [form="♀ (female)"]
  A10_RX = female pin header, 1 pin [form="♀ (female)"]
  A9_TX = female pin header, 1 pin [form="♀ (female)"]
  VCC_4 = female pin header, 1 pin [form="♀ (female)"]
  GND_10 = female pin header, 1 pin [form="♀ (female)"]
  GND_11 = female pin header, 1 pin [form="♀ (female)"]
  VCC_5 = female pin header, 1 pin [form="♀ (female)"]
  3_3V = female pin header, 1 pin [form="♀ (female)"]
  220 = Resistor [tolerance=±5% resistance=220 power=0.25 package="1206 [SMD]"]
  220_2 = Resistor [tolerance=±5% resistance=220 power=0.25 package="1206 [SMD]"]
  220_3 = Resistor [tolerance=±5% resistance=220 power=0.25 package="1206 [SMD]"]
  220_4 = Resistor [tolerance=±5% resistance=220 power=0.25 package="1206 [SMD]"]
  1k = Resistor [tolerance=±5% resistance=1k power=0.25 package="1206 [SMD]"]
  2k = Resistor [tolerance=±5% resistance=2k power=0.25 package="1206 [SMD]"]
  C9 = Ceramic Capacitor [capacitance=100nF voltage=35V package="100 mil [THT, multilayer]"]
  C10 = Ceramic Capacitor [capacitance=100nF voltage=35V package="100 mil [THT, multilayer]"]
  J1 = female pin header, 2 pins [form="♀ (female)"]
  B15 = female pin header, 1 pin [form="♀ (female)"]
  PWM = female pin header, 1 pin [form="♀ (female)"]
  A1 = female pin header, 1 pin [form="♀ (female)"]
  A0 = female pin header, 1 pin [form="♀ (female)"]
  C15 = female pin header, 1 pin [form="♀ (female)"]
  C14 = female pin header, 1 pin [form="♀ (female)"]
  C13 = female pin header, 1 pin [form="♀ (female)"]
  C16 = Ceramic Capacitor [capacitance=100nF voltage=35V package="100 mil [THT, multilayer]"]
  C17 = Ceramic Capacitor [capacitance=100nF voltage=35V package="100 mil [THT, multilayer]"]
  J4 = female pin header, 2 pins [form="♀ (female)"]
  ext_5v = female pin header, 2 pins [form="♀ (female)"]
  stepper_EN=A15 = female pin header, 2 pins [form="♀ (female)"]
  stepper_EN=A01 = female pin header, 2 pins [form="♀ (female)"]
  A15 = female pin header, 1 pin [form="♀ (female)"]
  GND_12 = female pin header, 4 pins [form="♀ (female)"]
  1_8k = Resistor [tolerance=±5% resistance=1.8k power=0.25 package="1206 [SMD]"]
  Steppers_ON = smd LED [color="Red (633nm)" current=0.030 package="1206 [SMD]"]
  2k_2 = Resistor [tolerance=±5% resistance=2k power=0.25 package="1206 [SMD]"]
  + = female pin header, 1 pin [form="♀ (female)"]
  C18 = Ceramic Capacitor [capacitance=100nF voltage=35V package="100 mil [THT, multilayer]"]
  C19 = Ceramic Capacitor [capacitance=100nF voltage=35V package="100 mil [THT, multilayer]"]
  C20 = Ceramic Capacitor [capacitance=100nF voltage=35V package="100 mil [THT, multilayer]"]
  C21 = Ceramic Capacitor [capacitance=100nF voltage=35V package="100 mil [THT, multilayer]"]
  C22 = Ceramic Capacitor [capacitance=100nF voltage=35V package="100 mil [THT, multilayer]"]
  C23 = Ceramic Capacitor [capacitance=100nF voltage=35V package="100 mil [THT, multilayer]"]
  C24 = Ceramic Capacitor [capacitance=100nF voltage=35V package="100 mil [THT, multilayer]"]
  C25 = Ceramic Capacitor [capacitance=100nF voltage=35V package="100 mil [THT, multilayer]"]
  C26 = Ceramic Capacitor [capacitance=100nF voltage=35V package="100 mil [THT, multilayer]"]
  C27 = Ceramic Capacitor [capacitance=100nF voltage=35V package="100 mil [THT, multilayer]"]
  GND_13 = female pin header, 1 pin [form="♀ (female)"]
  pullup = Resistor [tolerance=±5% resistance=220 power=0.25 package="1206 [SMD]"]
  5V_2 = female pin header, 1 pin [form="♀ (female)"]
  GND_14 = female pin header, 1 pin [form="♀ (female)"]
  DTR = female pin header, 1 pin [form="♀ (female)"]  # not connected
  5V_3 = female pin header, 1 pin [form="♀ (female)"]
  CTS = female pin header, 1 pin [form="♀ (female)"]  # not connected
  GND_15 = female pin header, 1 pin [form="♀ (female)"]

nets:
  N1: bluepill.B12, X.pin1, 220.Pin_1, C22.0
  N2: bluepill.B13, 1k.Pin_0, 2k.Pin_1
  N3: bluepill.B14, Z.pin1, 220_4.Pin_1, C21.0
  N4: bluepill.B15, B15.pin1
  N5: bluepill.A8, 74245_2.pin2
  N6: bluepill.A9, A9_TX.pin1
  N7: bluepill.A10, A10_RX.pin1
  N8: bluepill.A11, A11.pin1
  N9: bluepill.A12, A12.pin1
  N10: bluepill.A15, stepper_EN=A15.pin1, A15.pin1
  N11: bluepill.B3, COOLANT.pin1
  N12: bluepill.B4, COOLANT.pin2
  N13: bluepill.B5, CTRL_RESET.pin1, C23.0, pullup.Pin_0
  N14: bluepill.B6, FEED_HLD.pin1, C24.0
  N15: bluepill.B7, CYCLE_STRT.pin1, C25.0
  N16: bluepill.B8, DOOR.pin1, C26.0
  N17: bluepill.B9, -.pin1, 2k_2.Pin_0, C27.0
  N18: bluepill.5V, 5V.pin1, J4.pin1
  N19: bluepill.G, bluepill.GND, GND.pin1, 74LS08_(AND).pin7, 74LS32_(OR).pin7, 74245.pin10, 74245.pin19, C6.-, GND_2.pin1, GND_3.pin1, GND_4.pin1, GND_5.pin1, GND_6.pin1, C7.-, 74245_2.pin10, 74245_2.pin19, GND_7.pin1, GND_8.pin1, GND_9.pin1, GND_10.pin1, GND_11.pin1, 2k.Pin_0, C9.0, C10.0, C16.0, C17.0, ext_5v.pin1, GND_12.pin1, GND_12.pin2, GND_12.pin3, GND_12.pin4, 2k_2.Pin_1, C18.1, C19.1, C20.1, C21.1, C22.1, C23.1, C24.1, C25.1, C26.1, C27.1, GND_13.pin1, GND_14.pin1, GND_15.pin1
  N20: bluepill.3.3V, bluepill.3.3, C7.+, 3_3V.pin1, 220.Pin_0, 220_4.Pin_0, 1_8k.Pin_1, +.pin1, C18.0, pullup.Pin_1
  N21: bluepill.VBAT, VBAT.pin1
  N22: bluepill.C13, C13.pin1
  N23: bluepill.C14, C14.pin1
  N24: bluepill.C15, C15.pin1
  N25: bluepill.A0, A0.pin1
  N26: bluepill.A1, A1.pin1, stepper_EN=A01.pin1
  N27: bluepill.A2, 74245.pin7
  N28: bluepill.A3, 74245.pin6
  N29: bluepill.A4, 74LS08_(AND).pin1, 74LS08_(AND).pin4
  N30: bluepill.A5, 74LS32_(OR).pin1, 74LS32_(OR).pin4, 74245.pin3, 74245_2.pin8
  N31: bluepill.A6, 74245_2.pin6
  N32: bluepill.A7, 74245_2.pin5
  N33: bluepill.B0, 74245_2.pin4
  N34: bluepill.B1, 74245_2.pin3
  N35: bluepill.B10, B10.pin1
  N36: bluepill.B11, B11.pin1
  N37: bluepill.RST, RST.pin1
  N38: Y-L.pin1, 74LS32_(OR).pin2, 74LS32_(OR).pin13, 220_3.Pin_0, C19.0
  N39: Y-R.pin1, 74LS32_(OR).pin5, 74LS32_(OR).pin12, 220_2.Pin_0, C20.0
  N40: 74LS08_(AND).pin2, 74LS08_(AND).pin12, 74LS08_(AND).pin13, 74LS32_(OR).pin3
  N41: 74LS08_(AND).pin3, 74245.pin4
  N42: 74LS08_(AND).pin5, 74LS08_(AND).pin9, 74LS08_(AND).pin10, 74LS32_(OR).pin6
  N43: 74LS08_(AND).pin6, 74245_2.pin9
  N44: 74LS08_(AND).pin14, 74LS32_(OR).pin9, 74LS32_(OR).pin10, 74LS32_(OR).pin14, 74245.pin1, 74245.pin20, C6.+, 74245_2.pin1, 74245_2.pin20, 220_2.Pin_1, 220_3.Pin_1, C9.1, C10.1, J1.pin2, C16.1, C17.1, J4.pin2, ext_5v.pin2, 5V_2.pin1, 5V_3.pin1
  N45: 74LS32_(OR).pin11, 1k.Pin_1
  N46: 74245.pin2, 74245.pin5, 74245.pin8, 74245.pin9, 74245_2.pin7, stepper_EN=A15.pin2, stepper_EN=A01.pin2, Steppers_ON.cathode
  N47: 74245.pin12, EN_5.pin1
  N48: 74245.pin13, STEP_4.pin1
  N49: 74245.pin14, DIR_5.pin1
  N50: 74245.pin15, EN_4.pin1
  N51: 74245.pin16, STEP_3.pin1
  N52: 74245.pin17, DIR_4.pin1
  N53: 74245.pin18, EN_3.pin1
  N54: EN.pin1, 74245_2.pin13
  N55: DIR.pin1, 74245_2.pin15
  N56: STEP.pin1, 74245_2.pin14
  N57: EN_2.pin1, 74245_2.pin17
  N58: DIR_2.pin1, 74245_2.pin16
  N59: DIR_3.pin1, 74245_2.pin12
  N60: STEP_2.pin1, 74245_2.pin11
  N61: 74245_2.pin18, PWM.pin1
  N62: VCC.pin1, VCC_2.pin1, VCC_3.pin1, VCC_4.pin1, VCC_5.pin1, J1.pin1
  N63: 1_8k.Pin_0, Steppers_ON.anode

notes:
  mist
  flood
  ystep_R
  probe
  spindle
  Homing Sensors
  grbl/bluepill shield v3
  Marius Krabset 2022
  spindle EN
  spindle DIR
  Z DIR
  Z STEP
  Y STEP
  Y DIR
  X DIR
  X STEP
  stepper Z
  stepper Y-R
  stepper Y-L
  stepper X
  endstopVCC=5v
  Sensor Power
  ystep_L
  useMCU5v
  GND
  5V
  E-stop
  Serial
  enable
  PWM
